// Logisim project lab1.circ as structural Verilog
module gate_expr (
  input  a,
  input  b,
  input  c,
  input  e,
  input  f,
  output x
);

  wire and_1_out, not_1_out, or_1_out;

  not not_1 (not_1_out, b);
  and and_1 (and_1_out, a, not_1_out, c);
  or or_1 (or_1_out, e, f);
  nand nand_1 (x, and_1_out, or_1_out);
endmodule

module mux2 (
  input  D0,
  input  S,
  input  D1,
  output Y
);

  wire and_1_out, and_2_out, not_1_out;

  not not_1 (not_1_out, S);
  and and_1 (and_1_out, D0, not_1_out);
  and and_2 (and_2_out, S, D1);
  or or_1 (Y, and_1_out, and_2_out);
endmodule

module mux4 (
  input  D0,
  input  S0,
  input  D1,
  input  S1,
  input  D2,
  input  D3,
  output Y
);

  wire mux2_1_y, mux2_2_y;

  mux2 mux2_1 (.D0(D0), .S(S0), .D1(D1), .Y(mux2_1_y));
  mux2 mux2_2 (.D0(D2), .S(S0), .D1(D3), .Y(mux2_2_y));
  mux2 mux2_3 (.D0(mux2_1_y), .S(S1), .D1(mux2_2_y), .Y(Y));
endmodule

module priority8 (
  input  [7:0] I,
  input  EN,
  output F,
  output [2:0] Y,
  output C
);

  Priority_Encoder priority_encoder_1 (
    .in0(I[0]), .in1(I[1]), .in2(I[2]), .in3(I[3]), .in4(I[4]), .in5(I[5]), .in6(I[6]), .in7(I[7]), .out(Y),
    .en_in(EN), .gs(C), .en_out(F));
endmodule
